// Logisim project simGuia_0502.circ as structural Verilog: 1 circuit, main circuit main
module main (
  input  a,
  input  b,
  input  in_3,
  output s,
  output out_5
);

  wire nand_2_out;

  nand nand_1 (out_5, in_3, 1'b1);
  nand nand_2 (nand_2_out, a, 1'b1);
  nand nand_3 (s, nand_2_out, b);

  // Notes on the sheet:
  //   Porta Lógica not feita a partir de nand
  //   CIRCUITO FINAL
  //   not_a
endmodule
