// Logisim project simGuia_0503.circ as structural Verilog: 1 circuit, main circuit main
module main (
  input  a,
  input  b,
  input  in_3,
  output out_4,
  output out_5
);

  wire nor_1_out, nor_2_out, nor_4_out;

  nor nor_1 (nor_1_out, a, a);
  nor nor_2 (nor_2_out, b, b);
  nor nor_3 (out_5, in_3, in_3);
  nor nor_4 (nor_4_out, nor_1_out, nor_2_out);
  nor nor_5 (out_4, nor_4_out, nor_4_out);

  // Notes on the sheet:
  //   CIRCUITO FINAL
  //   Porta lógica NOT feita utilizando NOR
endmodule
