// Logisim project simGuia_0505.circ as structural Verilog: 1 circuit, main circuit main
module main (
  input  a,
  input  b,
  input  NOT_usando_NOR,
  input  OR_usando_NOR,
  input  in_5,
  output out_6,
  output out_7,
  output out_8
);

  wire nor_2_out, nor_3_out, nor_4_out, nor_6_out, nor_7_out, nor_8_out;

  nor nor_1 (out_7, NOT_usando_NOR, NOT_usando_NOR);
  nor nor_2 (nor_2_out, OR_usando_NOR, in_5);
  nor nor_3 (nor_3_out, a, a);
  nor nor_4 (nor_4_out, b, b);
  nor nor_5 (out_8, nor_2_out, nor_2_out);
  nor nor_6 (nor_6_out, nor_3_out, nor_4_out);
  nor nor_7 (nor_7_out, b, a);
  nor nor_8 (nor_8_out, nor_6_out, nor_7_out);
  nor nor_9 (out_6, nor_8_out, nor_8_out);

  // Notes on the sheet:
  //   SUBCIRCUITOS:
endmodule
