// Logisim project simGuia_0506.circ as structural Verilog: 1 circuit, main circuit main
module main (
  input  a,
  input  b,
  input  in_3,
  input  in_4,
  input  in_5,
  output out_6,
  output out_7,
  output out_8
);

  wire nand_1_out, nand_2_out, nand_4_out, nand_6_out, nand_7_out, nand_8_out;

  nand nand_1 (nand_1_out, a, 1'b1);
  nand nand_2 (nand_2_out, 1'b1, b);
  nand nand_3 (out_7, in_3, 1'b1);
  nand nand_4 (nand_4_out, in_4, in_5);
  nand nand_5 (out_8, nand_4_out, 1'b1);
  nand nand_6 (nand_6_out, a, b);
  nand nand_7 (nand_7_out, nand_1_out, nand_2_out);
  nand nand_8 (nand_8_out, nand_6_out, nand_7_out);
  nand nand_9 (out_6, nand_8_out, 1'b1);

  // Notes on the sheet:
  //   NOT a partir de NAND
  //   AND a partir de NAND
endmodule
