// Logisim project SIM_LEFT_SHIFT.circ as structural Verilog: 1 circuit, main circuit main
module main (
  input  LD,
  input  CLR,
  input  in_3
);

  wire and_1_out, clk_out, d_ff_2_q, d_ff_3_q, d_ff_4_q, d_ff_5_q, d_ff_6_q, undriven;

  Clock clk (.out(clk_out));
  D_Flip_Flop d_ff_1 (.clk(clk_out), .D(d_ff_2_q), .preset(undriven), .reset(CLR));  // open: Q, Qn
  D_Flip_Flop d_ff_2 (.clk(clk_out), .D(d_ff_3_q), .Q(d_ff_2_q), .reset(CLR));  // open: Qn, preset
  D_Flip_Flop d_ff_3 (.clk(clk_out), .D(d_ff_4_q), .Q(d_ff_3_q), .reset(CLR));  // open: Qn, preset
  D_Flip_Flop d_ff_4 (.clk(clk_out), .D(d_ff_5_q), .Q(d_ff_4_q), .reset(CLR));  // open: Qn, preset
  and and_1 (and_1_out, LD, in_3);
  D_Flip_Flop d_ff_5 (.clk(clk_out), .D(d_ff_6_q), .Q(d_ff_5_q), .reset(CLR));  // open: Qn, preset
  D_Flip_Flop d_ff_6 (.clk(clk_out), .D(1'b0), .Q(d_ff_6_q), .preset(and_1_out), .reset(CLR));  // open: Qn
endmodule
