// Logisim project SIM_LEFT_SHIFT_ALLBITS.circ as structural Verilog: 1 circuit, main circuit main
module main (
  input  LD,
  input  CLR,
  input  in_3,
  input  in_4,
  input  in_5,
  input  in_6,
  input  in_7,
  input  in_8
);

  wire and_1_out, and_2_out, and_3_out, and_4_out, and_5_out, and_6_out, clk_out, d_ff_2_q, d_ff_3_q,
       d_ff_4_q, d_ff_5_q, d_ff_6_q;

  Clock clk (.out(clk_out));
  and and_1 (and_1_out, LD, in_3);
  and and_2 (and_2_out, LD, in_4);
  D_Flip_Flop d_ff_1 (.clk(clk_out), .D(d_ff_2_q), .preset(and_1_out), .reset(CLR));  // open: Q, Qn
  and and_3 (and_3_out, LD, in_5);
  D_Flip_Flop d_ff_2 (.clk(clk_out), .D(d_ff_3_q), .Q(d_ff_2_q), .preset(and_2_out), .reset(CLR));  // open: Qn
  and and_4 (and_4_out, LD, in_6);
  D_Flip_Flop d_ff_3 (.clk(clk_out), .D(d_ff_4_q), .Q(d_ff_3_q), .preset(and_3_out), .reset(CLR));  // open: Qn
  and and_5 (and_5_out, LD, in_7);
  D_Flip_Flop d_ff_4 (.clk(clk_out), .D(d_ff_5_q), .Q(d_ff_4_q), .preset(and_4_out), .reset(CLR));  // open: Qn
  and and_6 (and_6_out, LD, in_8);
  D_Flip_Flop d_ff_5 (.clk(clk_out), .D(d_ff_6_q), .Q(d_ff_5_q), .preset(and_5_out), .reset(CLR));  // open: Qn
  D_Flip_Flop d_ff_6 (.clk(clk_out), .D(1'b0), .Q(d_ff_6_q), .preset(and_6_out), .reset(CLR));  // open: Qn

  // Notes on the sheet:
  //   DATA
endmodule
