// Logisim project SIM_LEFT_TWISTED_RING_SHIFT.circ as structural Verilog: 1 circuit, main circuit main
module main (
  input  LD,
  input  CLEAR,
  input  in_3
);

  wire and_1_out, CLK_out, d_ff_1_qn, d_ff_2_q, d_ff_3_q, d_ff_4_q, d_ff_5_q, d_ff_6_q;

  Clock CLK (.out(CLK_out));
  D_Flip_Flop d_ff_1 (.clk(CLK_out), .D(d_ff_2_q), .Qn(d_ff_1_qn), .reset(CLEAR));  // open: Q, preset
  D_Flip_Flop d_ff_2 (.clk(CLK_out), .D(d_ff_3_q), .Q(d_ff_2_q), .reset(CLEAR));  // open: Qn, preset
  D_Flip_Flop d_ff_3 (.clk(CLK_out), .D(d_ff_4_q), .Q(d_ff_3_q), .reset(CLEAR));  // open: Qn, preset
  D_Flip_Flop d_ff_4 (.clk(CLK_out), .D(d_ff_5_q), .Q(d_ff_4_q), .reset(CLEAR));  // open: Qn, preset
  D_Flip_Flop d_ff_5 (.clk(CLK_out), .D(d_ff_6_q), .Q(d_ff_5_q), .reset(CLEAR));  // open: Qn, preset
  and and_1 (and_1_out, in_3, LD);
  D_Flip_Flop d_ff_6 (.clk(CLK_out), .D(d_ff_1_qn), .Q(d_ff_6_q), .preset(and_1_out), .reset(CLEAR));  // open: Qn
endmodule
